// Logisim project Lab7Task2.circ as structural Verilog: 1 circuit, main circuit main
module main (
  input  Enable
);

  wire Clock_Signal__Press_Ctrl___T_out, j_k_ff_1_qn, j_k_ff_2_qn, j_k_ff_3_qn, j_k_ff_4_qn, j_k_ff_5_qn,
       j_k_ff_6_qn, j_k_ff_7_qn;
  wire [3:0] j_k_ff_1_q, j_k_ff_5_q;

  LED led_1 (.in(j_k_ff_1_q[1]));
  LED led_2 (.in(j_k_ff_1_q[0]));
  J_K_Flip_Flop j_k_ff_1 (
    .J(Enable), .clk(Clock_Signal__Press_Ctrl___T_out), .K(Enable), .Q(j_k_ff_1_q[0]), .Qn(j_k_ff_1_qn));  // open: preset, en, reset
  J_K_Flip_Flop j_k_ff_2 (
    .J(Enable), .clk(j_k_ff_1_qn), .K(Enable), .Q(j_k_ff_1_q[1]), .Qn(j_k_ff_2_qn));  // open: preset, en, reset
  Clock Clock_Signal__Press_Ctrl___T (.out(Clock_Signal__Press_Ctrl___T_out));
  LED led_3 (.in(j_k_ff_1_q[2]));
  J_K_Flip_Flop j_k_ff_3 (
    .J(Enable), .clk(j_k_ff_2_qn), .K(Enable), .Q(j_k_ff_1_q[2]), .Qn(j_k_ff_3_qn));  // open: preset, en, reset
  LED led_4 (.in(j_k_ff_1_q[3]));
  J_K_Flip_Flop j_k_ff_4 (
    .J(Enable), .clk(j_k_ff_3_qn), .K(Enable), .Q(j_k_ff_1_q[3]), .Qn(j_k_ff_4_qn));  // open: preset, en, reset
  LED led_5 (.in(j_k_ff_5_q[1]));
  LED led_6 (.in(j_k_ff_5_q[0]));
  J_K_Flip_Flop j_k_ff_5 (
    .J(Enable), .clk(j_k_ff_4_qn), .K(Enable), .Q(j_k_ff_5_q[0]), .Qn(j_k_ff_5_qn));  // open: preset, en, reset
  J_K_Flip_Flop j_k_ff_6 (
    .J(Enable), .clk(j_k_ff_5_qn), .K(Enable), .Q(j_k_ff_5_q[1]), .Qn(j_k_ff_6_qn));  // open: preset, en, reset
  LED led_7 (.in(j_k_ff_5_q[2]));
  J_K_Flip_Flop j_k_ff_7 (
    .J(Enable), .clk(j_k_ff_6_qn), .K(Enable), .Q(j_k_ff_5_q[2]), .Qn(j_k_ff_7_qn));  // open: preset, en, reset
  LED led_8 (.in(j_k_ff_5_q[3]));
  J_K_Flip_Flop j_k_ff_8 (.J(Enable), .clk(j_k_ff_7_qn), .K(Enable), .Q(j_k_ff_5_q[3]));  // open: Qn, preset, en, reset
  Hex_Digit_Display hex_digit_display_1 (.value(j_k_ff_5_q));  // open: dp
  Hex_Digit_Display hex_digit_display_2 (.value(j_k_ff_1_q));  // open: dp

  // Notes on the sheet:
  //   HEX display
endmodule
