// Logisim project Lab7Task3Divider.circ as structural Verilog: 1 circuit, main circuit main
module main (
  input  [7:0] Dividend_Upper,
  input  [7:0] Dividend_Lower,
  input  [7:0] Divisor,
  output [7:0] Quotient,
  output [7:0] Remainder
);

  Divider divider_1 (.a(Dividend_Lower), .b(Divisor), .out(Quotient), .upper(Dividend_Upper), .rem(Remainder));

  // Notes on the sheet:
  //   8 bit Divider
endmodule
