// Logisim project Lab7Task3Multiplier.circ as structural Verilog: 1 circuit, main circuit main
module main (
  input  [7:0] _8_bit_number_1,
  input  [7:0] _8_bit_number_2,
  output [7:0] _1st_8_digits_of_product__2_0_2_7_places,
  output [7:0] last_8_digits_of_product__2_8_2_15_places
);

  Multiplier multiplier_1 (
    .a(_8_bit_number_1), .b(_8_bit_number_2), .out(_1st_8_digits_of_product__2_0_2_7_places),
    .cout(last_8_digits_of_product__2_8_2_15_places));  // open: cin

  // Notes on the sheet:
  //   8-Bit Multiplier
endmodule
