// Logisim project Logisim Example.circ as structural Verilog: 1 circuit, main circuit main
module main (
  input  in_1,
  input  Use_Poke_tool__click_ME,
  input  in_3,
  input  Enable,
  input  in_5,
  input  in_6,
  input  in_7,
  input  in_8,
  output out_9,
  output out_10
);

  wire and_1_out, and_2_out, Clock_Signal__Press_Ctrl___T_out, j_k_ff_1_qn, j_k_ff_2_qn, j_k_ff_3_qn,
       not_1_out, not_2_out;
  wire [3:0] j_k_ff_2_q;

  LED led_1 (.in(j_k_ff_2_q[0]));
  LED led_2 (.in(j_k_ff_2_q[1]));
  J_K_Flip_Flop j_k_ff_1 (
    .J(Enable), .clk(j_k_ff_2_qn), .K(Enable), .Q(j_k_ff_2_q[1]), .Qn(j_k_ff_1_qn));  // open: preset, en, reset
  J_K_Flip_Flop j_k_ff_2 (
    .J(Enable), .clk(Clock_Signal__Press_Ctrl___T_out), .K(Enable), .Q(j_k_ff_2_q[0]), .Qn(j_k_ff_2_qn));  // open: preset, en, reset
  LED led_3 (.in(Use_Poke_tool__click_ME));
  LED led_4 (.in(j_k_ff_2_q[2]));
  J_K_Flip_Flop j_k_ff_3 (
    .J(Enable), .clk(j_k_ff_1_qn), .K(Enable), .Q(j_k_ff_2_q[2]), .Qn(j_k_ff_3_qn));  // open: preset, en, reset
  Clock Clock_Signal__Press_Ctrl___T (.out(Clock_Signal__Press_Ctrl___T_out));
  not not_1 (not_1_out, in_3);
  LED led_5 (.in(j_k_ff_2_q[3]));
  J_K_Flip_Flop j_k_ff_4 (.J(Enable), .clk(j_k_ff_3_qn), .K(Enable), .Q(j_k_ff_2_q[3]));  // open: Qn, preset, en, reset
  not not_2 (not_2_out, in_1);
  Hex_Digit_Display hex_digit_display_1 (.value(j_k_ff_2_q));  // open: dp
  and and_1 (and_1_out, not_2_out, in_3);
  and and_2 (and_2_out, in_1, not_1_out);
  Hex_Digit_Display hex_digit_display_2 (.value({in_8, in_7, in_6, in_5}));  // open: dp
  xor xor_1 (out_10, and_1_out, and_2_out);
  LED led_6 (.in(out_10));

  assign out_9 = Use_Poke_tool__click_ME;

  // Notes on the sheet:
  //   Connect ADDER and display
  //   HEX display
endmodule
